# Fritzing sketch 02_breadboard (saved by Fritzing 0.9.4)
breadboards: 1

parts:
  Teensy_3_1 = Teensy 3.1
  R1 = Resistor [tolerance=±5% resistance=220 package=THT]
  R2 = Resistor [tolerance=±5% resistance=220 package=THT]
  R3 = Resistor [tolerance=±5% resistance=220 package=THT]
  LED1 = LED - 5mm [color="Red (633nm)" package="5 mm [THT]"]
  LED2 = LED - 5mm [color="Green (565nm)" package="5 mm [THT]"]
  LED3 = LED - 5mm [color="Blue (430nm)" package="5 mm [THT]"]
  R4 = Resistor [tolerance=±5% resistance=220 package=THT]
  S1 = Pushbutton [package="[THT]"]

nets:
  N1: Teensy_3_1.GND, R1.Pin_1, R2.Pin_1, R3.Pin_1, R4.Pin_1
  N2: Teensy_3_1.3V3, S1.Pin_1, S1.Pin_2
  N3: R1.Pin_0, LED1.anode
  N4: R2.Pin_0, LED2.anode
  N5: R3.Pin_0, LED3.anode
  N6: R4.Pin_0, S1.Pin_3, S1.Pin_4
